# Fritzing sketch LED_Bluetooth (saved by Fritzing 0.9.7b)
breadboards: 1

parts:
  R1 = Resistor [tolerance=±5% power=0.25 resistance=220 package=THT]
  Mod1 = Heltec WiFi LoRa 32 V2 [part_number=HTIT-WB32LA]
  LED1 = LED - 5mm [color="Red (633nm)" current=0.030 package="5 mm [THT]"]

nets:
  N1: R1.Pin_0, Mod1.GND
  N2: R1.Pin_1, LED1.cathode
  N3: Mod1.pin_27, LED1.anode
