# Fritzing sketch LED_Bluetooth_4 (saved by Fritzing 0.9.7b)
breadboards: 1

parts:
  LED1 = LED - 5mm [color="Blue (430nm)" current=0.030 package="5 mm [THT]"]
  LED2 = LED - 5mm [color="Blue (430nm)" current=0.030 package="5 mm [THT]"]
  LED3 = LED - 5mm [color="Blue (430nm)" current=0.030 package="5 mm [THT]"]
  LED4 = LED - 5mm [color="Blue (430nm)" current=0.030 package="5 mm [THT]"]
  R1 = Resistor [tolerance=±5% power=0.25 resistance=200 package=THT]
  R2 = Resistor [tolerance=±5% power=0.25 resistance=200 package=THT]
  R3 = Resistor [tolerance=±5% power=0.25 resistance=200 package=THT]
  R4 = Resistor [tolerance=±5% power=0.25 resistance=200 package=THT]
  Mod1 = Heltec WiFi LoRa 32 V2 [part_number=HTIT-WB32LA]

nets:
  N1: LED1.cathode, R4.Pin_1
  N2: LED1.anode, Mod1.pin_1
  N3: LED2.cathode, R3.Pin_1
  N4: LED2.anode, Mod1.pin_27
  N5: LED3.cathode, R1.Pin_1
  N6: LED3.anode, Mod1.pin_28
  N7: LED4.cathode, R2.Pin_1
  N8: LED4.anode, Mod1.pin_29
  N9: R1.Pin_0, R2.Pin_0, R3.Pin_0, R4.Pin_0, Mod1.GND
