# Fritzing sketch LCD_AI (saved by Fritzing 0.9.7b)
breadboards: 1

parts:
  부품1 = LCD1602-I2C
  Mod1 = Heltec WiFi LoRa 32 V2 [part_number=HTIT-WB32LA]

nets:
  GND: 부품1.GND, Mod1.GND
  N1: 부품1.VCC, Mod1.pin_20
  N2: 부품1.SDA, Mod1.pin_1
  N3: 부품1.SCL, Mod1.pin_27

custom parts:
  LCD1602-I2C: A standard character display, usually with 2x16 characters. Comes in many colors with LCM1602 IIC attached.
