# Fritzing sketch RIP (saved by Fritzing 0.9.7b)
breadboards: 1

parts:
  R1 = Resistor [tolerance=±5% power=0.25 resistance=200 package=THT]
  LED1 = LED - 5mm [color="Blue (430nm)" current=0.030 package="5 mm [THT]"]
  Mod1 = Heltec WiFi LoRa 32 V2 [part_number=HTIT-WB32LA]
  부품1 = HC-SR501 Body Sensor Module

nets:
  N1: R1.Pin_0, LED1.anode
  N2: R1.Pin_1, Mod1.pin_3
  GND: LED1.cathode, Mod1.GND, 부품1.GND
  N3: Mod1.pin_2, 부품1.OUT
  N4: Mod1.pin_20, 부품1.VCC

custom parts:
  HC-SR501 Body Sensor Module: Pyroelectric Infrared PIR Motion Sensor Detector Module
